# Fritzing sketch arduinoTi_trigger_dual (saved by Fritzing 0.9.2b)

parts:
  BNC_OUT = BNC [package=bnc]
  part = IC, DIP package, 16 pins [chip_label=SN74LS138]
  part_2 = Arduino Uno (Rev3)
  DB15HD = female pin header, 15 pins [form="♀ (female)"]
  BNC_TRIGGER = BNC [package=bnc]
  S1 = HALL-EFFECT-SENSOR [package=to-92]
  S2 = HALL-EFFECT-SENSOR [package=to-92]
  S3 = HALL-EFFECT-SENSOR [package=to-92]

nets:
  GND: BNC_OUT.GND, part.pin4, part.pin5, part.pin8, part_2.GND, DB15HD.pin6, DB15HD.pin7, DB15HD.pin8, DB15HD.pin10, BNC_TRIGGER.GND, S1.GND, S2.GND, S3.GND
  N1: BNC_OUT.OUT, part_2.D13/SCK
  N2: part.pin1, part_2.D8
  N3: part.pin2, part_2.D9_PWM
  N4: part.pin3, part_2.D10_PWM/SS
  VCC: part.pin6, part.pin16, part_2.5V, S1.VCC, S2.VCC, S3.VCC
  N5: part.pin9, DB15HD.pin1
  N6: part.pin10, DB15HD.pin2
  N7: part.pin11, DB15HD.pin11
  N8: part.pin12, DB15HD.pin3
  N9: part.pin13, DB15HD.pin12
  N10: part.pin14, DB15HD.pin13
  N11: part_2.A0, S1.OUT
  N12: part_2.A1, S2.OUT
  N13: part_2.A2, S3.OUT
  N14: part_2.D2, BNC_TRIGGER.OUT

custom parts:
  HALL-EFFECT-SENSOR: TO-92 hall effect sensor
