# Fritzing sketch arduinoTi_trigger_dual (saved by Fritzing 0.9.2b)

parts:
  BNC_OUT = BNC [package=bnc]
  IC1 = IC, DIP package, 16 pins [chip_label=CD74HCT138]
  Part1 = Arduino Uno (Rev3)
  DB15HD = female pin header, 15 pins [form="♀ (female)"]
  BNC_TRIGGER = BNC [package=bnc]
  S1 = HALL-EFFECT-SENSOR [package=to-92]
  S2 = HALL-EFFECT-SENSOR [package=to-92]
  S3 = HALL-EFFECT-SENSOR [package=to-92]
  IC2 = IC, DIP package, 14 pins [chip_label=MC74HC04N]
  R2 = Resistor [tolerance=±5% resistance=10k package=THT]
  R1 = Resistor [tolerance=±5% resistance=10k package=THT]
  Q1 = MOSFET-NCHANNEL [part_number=BS170 package=dpak]

nets:
  GND: BNC_OUT.GND, IC1.pin4, IC1.pin5, IC1.pin8, Part1.GND, DB15HD.pin6, DB15HD.pin7, DB15HD.pin8, DB15HD.pin10, BNC_TRIGGER.GND, S1.GND, S2.GND, S3.GND, IC2.pin7
  N1: BNC_OUT.OUT, IC2.pin2
  N2: IC1.pin1, Part1.D8
  N3: IC1.pin2, Part1.D9_PWM
  N4: IC1.pin3, Part1.D10_PWM/SS
  VCC: IC1.pin6, IC1.pin16, Part1.5V, S1.VCC, S2.VCC, S3.VCC, IC2.pin14, R2.Pin_0
  N5: IC1.pin7, IC2.pin1
  N6: IC1.pin9, DB15HD.pin1
  N7: IC1.pin10, DB15HD.pin2
  N8: IC1.pin11, DB15HD.pin11
  N9: IC1.pin12, DB15HD.pin3
  N10: IC1.pin13, DB15HD.pin12
  N11: IC1.pin14, DB15HD.pin13
  N12: Part1.A0, S1.OUT
  N13: Part1.A1, S2.OUT
  N14: Part1.A2, S3.OUT
  N15: Part1.D2, R2.Pin_1, Q1.D
  N16: Part1.3V3, R1.Pin_0, Q1.G
  N17: BNC_TRIGGER.OUT, R1.Pin_1, Q1.S

custom parts:
  HALL-EFFECT-SENSOR: TO-92 hall effect sensor
